// Logisim project Projet.circ as structural Verilog: 38 circuits, main circuit main
module main (
  input  Auto_run,
  input  [11:0] Manual_Command,
  input  Manal_Input,
  input  Enable,
  input  [3:0] Input,
  input  [3:0] Set_R1,
  input  [3:0] Set_R0,
  output [5:0] out_8
);

  wire and_3_out, and_4_out, and_6_out, automate_ctrl_entry_1_alu_enable,
       automate_ctrl_entry_1_enable_ram_output, automate_ctrl_entry_1_enable_sortie_alu,
       automate_ctrl_entry_1_flush, automate_ctrl_entry_1_pc_write_external, automate_ctrl_entry_1_ram_write,
       automate_ctrl_entry_1_reset_registre_cible, clock_1_out, Ena_out, inc_registre_ext_1_cout, L_out,
       MR_out, not_1_out, not_2_out, or_2_out, or_3_out, or_4_out, or_5_out, or_6_out, or_8_out, R_2_out,
       R_out;
  wire [1:0] ctrl_v2_1_res;
  wire [2:0] alu_4bits_simplified_1_flag_out;
  wire [3:0] alu_4bits_simplified_1_output, alu_input_selecter_simplified_1_s,
       alu_input_selecter_simplified_2_s, alu_input_selecter_simplified_comp_1_s, and_1_out, and_2_out,
       and_5_out, clocked_register_4_1_output, ctrl_v2_1_operation, inc_registre_ext_1_pc_count, or_1_out,
       ram_1_data_out, registre_selection_simplified_1_r0, registre_selection_simplified_1_r1,
       registre_selection_simplified_1_r2, registre_selection_simplified_1_r3;
  wire [3:3] Force_set_Memory_out, or_7_out;
  wire [11:0] multiplexer_1_out, rom_1_data;

  Alu_input_selecter_simplified alu_input_selecter_simplified_1 (
    .S(alu_input_selecter_simplified_1_s), .R3(registre_selection_simplified_1_r3),
    .R2(registre_selection_simplified_1_r2), .R1(registre_selection_simplified_1_r1),
    .R0(registre_selection_simplified_1_r0), .Selection(ctrl_v2_1_res), .ENABLE(1'b1));
  assign or_1_out = ram_1_data_out | Input | and_5_out;  // OR_Gate or_1, 4 bits wide
  Button R (.out(R_out));
  or or_2 (or_2_out, R_out, automate_ctrl_entry_1_reset_registre_cible);
  Button MR (.out(MR_out));
  Registre_Selection_simplified registre_selection_simplified_1 (
    .RESET(or_2_out), .R0(registre_selection_simplified_1_r0), .R1(registre_selection_simplified_1_r1),
    .Input(or_1_out), .R_Selecter(ctrl_v2_1_res), .Master_Reset(MR_out), .Set_R0(and_1_out),
    .Set_R1(and_2_out), .R2(registre_selection_simplified_1_r2), .R3(registre_selection_simplified_1_r3));
  assign and_1_out = {4{Force_set_Memory_out[3]}} & Set_R0;  // AND_Gate and_1, 4 bits wide
  assign and_2_out = Set_R1 & {4{Force_set_Memory_out[3]}};  // AND_Gate and_2, 4 bits wide
  Button Force_set_Memory (.out(Force_set_Memory_out[3]));
  or or_3 (or_3_out, MR_out, automate_ctrl_entry_1_flush);
  Ram ram_1 (
    .Data_in(alu_input_selecter_simplified_1_s), .Write(automate_ctrl_entry_1_ram_write), .Address(out_8),
    .Reset_writing_state(or_3_out), .Data_out(ram_1_data_out), .CLK(clock_1_out),
    .Enable_output(automate_ctrl_entry_1_enable_ram_output));
  Hex_Digit_Display hex_digit_display_1 (.value(registre_selection_simplified_1_r0));  // open: dp
  Hex_Digit_Display hex_digit_display_2 (.value(registre_selection_simplified_1_r1));  // open: dp
  or or_4 (or_4_out, Enable, automate_ctrl_entry_1_alu_enable);
  Alu_input_selecter_simplified alu_input_selecter_simplified_2 (
    .S(alu_input_selecter_simplified_2_s), .R3(registre_selection_simplified_1_r3),
    .R2(registre_selection_simplified_1_r2), .R1(registre_selection_simplified_1_r1),
    .R0(registre_selection_simplified_1_r0), .Selection(out_8[5:4]), .ENABLE(or_4_out));
  Alu_input_selecter_simplified_comp alu_input_selecter_simplified_comp_1 (
    .S(alu_input_selecter_simplified_comp_1_s), .R3(registre_selection_simplified_1_r3),
    .R2(registre_selection_simplified_1_r2), .R1(registre_selection_simplified_1_r1),
    .R0(registre_selection_simplified_1_r0), .Selection(out_8[3:2]), .Complement(out_8[1]), .ENABLE(or_4_out));
  and and_3 (and_3_out, automate_ctrl_entry_1_flush, not_1_out);
  or or_5 (or_5_out, and_3_out, automate_ctrl_entry_1_pc_write_external);
  Inc_Registre_Ext inc_registre_ext_1 (
    .External_line_input(out_8[5:2]), .Cout(inc_registre_ext_1_cout), .PC_Count(inc_registre_ext_1_pc_count),
    .External_Write(automate_ctrl_entry_1_pc_write_external), .CLK(or_5_out));
  not not_1 (not_1_out, Manal_Input);
  Hex_Digit_Display hex_digit_display_3 (.value(alu_input_selecter_simplified_comp_1_s));  // open: dp
  Multiplexer #(.width(12)) multiplexer_1 (
    .in0(rom_1_data), .in1(Manual_Command), .out(multiplexer_1_out), .sel(Manal_Input));  // open: en
  CTRL_V2 ctrl_v2_1 (
    .Rin_12(multiplexer_1_out), .Operation(ctrl_v2_1_operation), .A(out_8[5:4]), .Res(ctrl_v2_1_res),
    .Ext(out_8[1:0]), .B(out_8[3:2]));
  and and_4 (and_4_out, out_8[0], automate_ctrl_entry_1_alu_enable);
  Hex_Digit_Display hex_digit_display_4 (.value(alu_input_selecter_simplified_2_s));  // open: dp
  ROM #(.addrWidth(4), .dataWidth(12)) rom_1 (.addr(inc_registre_ext_1_pc_count), .data(rom_1_data));  // open: sel
  Alu_4bits_simplified alu_4bits_simplified_1 (
    .Cin(and_4_out), .IN_B(alu_input_selecter_simplified_comp_1_s), .IN_A(alu_input_selecter_simplified_2_s),
    .OUTPUT(alu_4bits_simplified_1_output), .CTRL(ctrl_v2_1_operation[1:0]),
    .CLK(automate_ctrl_entry_1_alu_enable), .FLAG_OUT(alu_4bits_simplified_1_flag_out));
  Button R_2 (.out(R_2_out));
  or or_6 (or_6_out, R_2_out, automate_ctrl_entry_1_flush);
  Hex_Digit_Display hex_digit_display_5 (.value(alu_4bits_simplified_1_output));  // open: dp
  DotMatrix #(.matrixcols(1), .matrixrows(3)) dotmatrix_1 (.col0(alu_4bits_simplified_1_flag_out));
  Hex_Digit_Display hex_digit_display_6 (.value(clocked_register_4_1_output));  // open: dp
  Clocked_register_4 clocked_register_4_1 (
    .Set_4(alu_4bits_simplified_1_output), .Output(clocked_register_4_1_output), .Reset(or_6_out),
    .CLK(clock_1_out));
  Button Ena (.out(Ena_out));
  or or_7 (or_7_out[3], Ena_out, automate_ctrl_entry_1_enable_sortie_alu);
  assign and_5_out = clocked_register_4_1_output & {4{or_7_out[3]}};  // AND_Gate and_5, 4 bits wide
  not not_2 (not_2_out, inc_registre_ext_1_cout);
  and and_6 (and_6_out, not_2_out, Auto_run);
  Clock clock_1 (.out(clock_1_out));
  Button L (.out(L_out));
  or or_8 (or_8_out, and_6_out, L_out);
  Automate_ctrl_Entry automate_ctrl_entry_1 (
    .CLK(clock_1_out), .Launch(or_8_out), .Alu_Enable(automate_ctrl_entry_1_alu_enable),
    .Reset_registre_cible(automate_ctrl_entry_1_reset_registre_cible),
    .Enable_Sortie_Alu(automate_ctrl_entry_1_enable_sortie_alu), .Ram_Write(automate_ctrl_entry_1_ram_write),
    .Enable_Ram_Output(automate_ctrl_entry_1_enable_ram_output), .FLUSH(automate_ctrl_entry_1_flush),
    .Ctrl_IN(ctrl_v2_1_operation[3:2]), .PC_Write_External(automate_ctrl_entry_1_pc_write_external),
    .EXT_JUMP_CTRL(out_8[1:0]), .FLAG_IN(alu_4bits_simplified_1_flag_out));

  // Notes on the sheet:
  //   Utilisé comme Mux 4
  //   Visualisation IMM
  //   contents of rom_1 (hex, n*v repeats v):
  //   c0d 4 c00
  //   Registre temporaire
  //   Flags :
  //   OV
  //   NZ
  //   ZF
  //   Launch
endmodule

module RS (
  input  S,
  input  R,
  output Q
);

  wire nor_1_out;

  nor nor_1 (nor_1_out, S, Q);
  nor nor_2 (Q, nor_1_out, R);
endmodule

// REG4
module Registre_4_bits (
  input  S3,
  input  S2,
  input  S1,
  input  S0,
  input  Reset,
  output S0_2,
  output S1_2,
  output S2_2,
  output S3_2
);

  RS rs_1 (.S(S0), .R(Reset), .Q(S0_2));
  RS rs_2 (.S(S1), .R(Reset), .Q(S1_2));
  RS rs_3 (.S(S2), .R(Reset), .Q(S2_2));
  RS rs_4 (.S(S3), .R(Reset), .Q(S3_2));
endmodule

module Mux_4 (
  input  selA,
  input  selB,
  input  A,
  input  B,
  input  C,
  input  D,
  output Q
);

  wire and_1_out, and_2_out, and_3_out, and_4_out, not_1_out, not_2_out;

  not not_1 (not_1_out, selA);
  not not_2 (not_2_out, selB);
  and and_1 (and_1_out, A, not_2_out, not_1_out);
  and and_2 (and_2_out, B, not_2_out, selA);
  and and_3 (and_3_out, C, not_1_out, selB);
  and and_4 (and_4_out, D, selB, selA);
  or or_1 (Q, and_1_out, and_2_out, and_3_out, and_4_out);
endmodule

module Full_adder (
  input  A,
  input  B,
  input  Cin,
  output S,
  output Cout
);

  wire and_1_out, and_2_out, xor_1_out;

  xor xor_1 (xor_1_out, A, B);
  xor xor_2 (S, xor_1_out, Cin);
  and and_1 (and_1_out, xor_1_out, Cin);
  and and_2 (and_2_out, A, B);
  or or_1 (Cout, and_1_out, and_2_out);
endmodule

module DEMUX (
  input  SelA,
  input  SelB,
  input  E,
  output S0,
  output S1,
  output S2,
  output S3
);

  wire not_1_out, not_2_out;

  not not_1 (not_1_out, SelA);
  not not_2 (not_2_out, SelB);
  and and_1 (S0, not_1_out, E, not_2_out);
  and and_2 (S1, SelA, E, not_2_out);
  and and_3 (S2, not_1_out, E, SelB);
  and and_4 (S3, SelA, E, SelB);
endmodule

module Alu_1bit (
  input  A,
  input  B,
  input  Cin,
  input  Sel_B,
  input  Sel_A,
  output Cout,
  output S
);

  wire and_1_out, Cin_out, full_adder_1_s, or_1_out;

  or or_1 (or_1_out, B, A);
  and and_1 (and_1_out, B, A);
  Full_adder full_adder_1 (.A(B), .B(A), .Cin(Cin), .S(full_adder_1_s), .Cout(Cout));
  xor u_Cin (Cin_out, B, A);
  Mux_4 mux_4_1 (.selA(Sel_A), .selB(Sel_B), .A(full_adder_1_s), .B(or_1_out), .C(and_1_out), .D(Cin_out), .Q(S));
endmodule

module Alu_4bits (
  input  Sel_B,
  input  Sel_A,
  input  A0,
  input  B0,
  input  Cin,
  input  A1,
  input  B1,
  input  A2,
  input  B2,
  input  A3,
  input  B3,
  output S0,
  output S1,
  output S2,
  output S3,
  output Cout
);

  wire alu_1bit_1_cout, alu_1bit_2_cout, alu_1bit_3_cout;

  Alu_1bit alu_1bit_1 (.Cout(alu_1bit_1_cout), .S(S0), .A(A0), .B(B0), .Cin(Cin), .Sel_B(Sel_B), .Sel_A(Sel_A));
  Alu_1bit alu_1bit_2 (
    .Cout(alu_1bit_2_cout), .S(S1), .A(A1), .B(B1), .Cin(alu_1bit_1_cout), .Sel_B(Sel_B), .Sel_A(Sel_A));
  Alu_1bit alu_1bit_3 (
    .Cout(alu_1bit_3_cout), .S(S2), .A(A2), .B(B2), .Cin(alu_1bit_2_cout), .Sel_B(Sel_B), .Sel_A(Sel_A));
  Alu_1bit alu_1bit_4 (.Cout(Cout), .S(S3), .A(A3), .B(B3), .Cin(alu_1bit_3_cout), .Sel_B(Sel_B), .Sel_A(Sel_A));
endmodule

module Registre___Selection (
  input  S3,
  input  S2,
  input  S1,
  input  S0,
  input  S1_2,
  input  S0_2,
  input  In_0,
  input  In_1,
  input  In_2,
  input  In_3,
  input  RESET,
  input  S3_2,
  input  S2_2,
  input  S1_3,
  input  S0_3,
  output R0_0,
  output R0_1,
  output R0_2,
  output R0_3,
  output R1_0,
  output R1_1,
  output R1_2,
  output R1_3
);

  wire demux_1_s0, demux_1_s1, demux_2_s0, demux_2_s1, demux_3_s0, demux_3_s1, demux_4_s0, demux_4_s1,
       demux_5_s0, demux_5_s1, or_1_out, or_2_out, or_3_out, or_4_out, or_5_out, or_6_out, or_7_out, or_8_out;

  DEMUX demux_1 (.E(In_0), .SelA(S0_2), .SelB(S1_2), .S0(demux_1_s0), .S1(demux_1_s1));  // open: S2, S3
  DEMUX demux_2 (.E(In_1), .SelA(S0_2), .SelB(S1_2), .S0(demux_2_s0), .S1(demux_2_s1));  // open: S2, S3
  DEMUX demux_3 (.E(In_2), .SelA(S0_2), .SelB(S1_2), .S0(demux_3_s0), .S1(demux_3_s1));  // open: S2, S3
  DEMUX demux_4 (.E(In_3), .SelA(S0_2), .SelB(S1_2), .S0(demux_4_s0), .S1(demux_4_s1));  // open: S2, S3
  DEMUX demux_5 (.E(RESET), .SelA(S0_2), .SelB(S1_2), .S0(demux_5_s0), .S1(demux_5_s1));  // open: S2, S3
  or or_1 (or_1_out, S0, demux_1_s0);
  or or_2 (or_2_out, S1, demux_2_s0);
  or or_3 (or_3_out, S2, demux_3_s0);
  or or_4 (or_4_out, S3, demux_4_s0);
  or or_5 (or_5_out, S0_3, demux_1_s1);
  or or_6 (or_6_out, S1_3, demux_2_s1);
  or or_7 (or_7_out, S2_2, demux_3_s1);
  or or_8 (or_8_out, S3_2, demux_4_s1);
  Registre_4_bits registre_4_bits_1 (
    .Reset(demux_5_s0), .S3(or_4_out), .S2(or_3_out), .S1(or_2_out), .S0(or_1_out), .S0_2(R0_0), .S1_2(R0_1),
    .S2_2(R0_2), .S3_2(R0_3));
  Registre_4_bits registre_4_bits_2 (
    .Reset(demux_5_s1), .S3(or_8_out), .S2(or_7_out), .S1(or_6_out), .S0(or_5_out), .S0_2(R1_0), .S1_2(R1_1),
    .S2_2(R1_2), .S3_2(R1_3));
endmodule

module Demux_8 (
  input  In,
  input  Sel2,
  input  Sel1,
  input  Sel0,
  output S0,
  output S1,
  output S2,
  output S3,
  output S4,
  output S5,
  output S6,
  output S7
);

  wire not_1_out, not_2_out, not_3_out;

  not not_1 (not_1_out, Sel2);
  not not_2 (not_2_out, Sel1);
  not not_3 (not_3_out, Sel0);
  and and_1 (S0, In, not_1_out, not_2_out, not_3_out);
  and and_2 (S1, In, not_1_out, not_2_out, Sel0);
  and and_3 (S2, In, not_1_out, Sel1, not_3_out);
  and and_4 (S3, In, not_1_out, Sel1, Sel0);
  and and_5 (S4, In, Sel2, not_2_out, not_3_out);
  and and_6 (S5, In, Sel2, not_2_out, Sel0);
  and and_7 (S6, In, Sel2, Sel1, not_3_out);
  and and_8 (S7, In, Sel2, Sel1, Sel0);
endmodule

module Automate (
  input  CLK,
  input  Launch,
  output _7,
  output _6,
  output _5,
  output _4,
  output _3,
  output _2,
  output _1,
  output _0
);

  wire and_1_out, and_2_out, and_3_out, and_4_out, and_5_out, and_6_out, and_7_out, and_8_out, and_9_out,
       d_ff_1_q, d_ff_1_qn, d_ff_2_q, d_ff_2_qn, d_ff_3_q, d_ff_3_qn, not_1_out, not_2_out, not_3_out,
       not_4_out, not_5_out, not_6_out, not_7_out, not_8_out, not_9_out, not_10_out, or_1_out, or_2_out,
       rs_1_q;

  RS rs_1 (.S(Launch), .R(_7), .Q(rs_1_q));
  and and_1 (and_1_out, CLK, rs_1_q);
  not not_1 (not_1_out, not_2_out);
  not not_2 (not_2_out, CLK);
  not not_3 (not_3_out, not_1_out);
  not not_4 (not_4_out, not_3_out);
  not not_5 (not_5_out, d_ff_1_q);
  not not_6 (not_6_out, d_ff_2_q);
  not not_7 (not_7_out, d_ff_1_q);
  not not_8 (not_8_out, d_ff_1_q);
  not not_9 (not_9_out, d_ff_2_q);
  not not_10 (not_10_out, d_ff_3_q);
  and and_2 (and_2_out, not_5_out, and_1_out);
  and and_3 (and_3_out, d_ff_1_q, not_6_out);
  and and_4 (and_4_out, not_7_out, d_ff_2_q);
  and and_5 (and_5_out, not_8_out, d_ff_3_q);
  and and_6 (and_6_out, not_9_out, d_ff_3_q);
  and and_7 (and_7_out, d_ff_1_q, d_ff_2_q, not_10_out);
  or or_1 (or_1_out, and_3_out, and_4_out);
  or or_2 (or_2_out, and_5_out, and_6_out, and_7_out);
  and and_8 (and_8_out, or_1_out, and_1_out);
  and and_9 (and_9_out, or_2_out, and_1_out);
  D_Flip_Flop d_ff_1 (.clk(not_4_out), .D(and_2_out), .Q(d_ff_1_q), .Qn(d_ff_1_qn));  // open: preset, en, reset
  D_Flip_Flop d_ff_2 (.clk(not_4_out), .D(and_8_out), .Q(d_ff_2_q), .Qn(d_ff_2_qn));  // open: preset, en, reset
  D_Flip_Flop d_ff_3 (.clk(not_4_out), .D(and_9_out), .Q(d_ff_3_q), .Qn(d_ff_3_qn));  // open: preset, en, reset
  Decodeur_8 decodeur_8_1 (
    .S0(_0), .S1(_1), .S2(_2), .S3(_3), .S4(_4), .S5(_5), .S6(_6), .S7(_7), .Sel2(d_ff_3_q), .Sel1(d_ff_2_q),
    .Sel0(d_ff_1_q));

  // Notes on the sheet:
  //   Uilisé pour créer un delay (Bascule D réglées en rising edge pour eviter toute oscillation
endmodule

module Decodeur_8 (
  input  Sel2,
  input  Sel1,
  input  Sel0,
  output S0,
  output S1,
  output S2,
  output S3,
  output S4,
  output S5,
  output S6,
  output S7
);

  wire not_1_out, not_2_out, not_3_out;

  not not_1 (not_1_out, Sel2);
  not not_2 (not_2_out, Sel1);
  not not_3 (not_3_out, Sel0);
  and and_1 (S0, 1'b1, not_1_out, not_2_out, not_3_out);
  and and_2 (S1, 1'b1, not_1_out, not_2_out, Sel0);
  and and_3 (S2, 1'b1, not_1_out, Sel1, not_3_out);
  and and_4 (S3, 1'b1, not_1_out, Sel1, Sel0);
  and and_5 (S4, 1'b1, Sel2, not_2_out, not_3_out);
  and and_6 (S5, 1'b1, Sel2, not_2_out, Sel0);
  and and_7 (S6, 1'b1, Sel2, Sel1, not_3_out);
  and and_8 (S7, 1'b1, Sel2, Sel1, Sel0);
endmodule

module Alu_input_selecter (
  input  SelB,
  input  SelA,
  input  ENABLE,
  input  R3_3,
  input  R2_3,
  input  R1_3,
  input  R0_3,
  input  R3_2,
  input  R2_2,
  input  R1_2,
  input  R0_2,
  input  R3_1,
  input  R2_1,
  input  R1_1,
  input  R0_1,
  input  R3_0,
  input  R2_0,
  input  R1_0,
  input  R0_0,
  output S0,
  output S1,
  output S2,
  output S3
);

  wire mux_4_1_q, mux_4_2_q, mux_4_3_q, mux_4_4_q;

  Mux_4 mux_4_1 (.selA(SelA), .selB(SelB), .A(R0_0), .B(R1_0), .C(R2_0), .D(R3_0), .Q(mux_4_1_q));
  Mux_4 mux_4_2 (.selA(SelA), .selB(SelB), .A(R0_1), .B(R1_1), .C(R2_1), .D(R3_1), .Q(mux_4_2_q));
  Mux_4 mux_4_3 (.selA(SelA), .selB(SelB), .A(R0_2), .B(R1_2), .C(R2_2), .D(R3_2), .Q(mux_4_3_q));
  Mux_4 mux_4_4 (.selA(SelA), .selB(SelB), .A(R0_3), .B(R1_3), .C(R2_3), .D(R3_3), .Q(mux_4_4_q));
  and and_1 (S0, mux_4_1_q, ENABLE);
  and and_2 (S1, mux_4_2_q, ENABLE);
  and and_3 (S2, mux_4_3_q, ENABLE);
  and and_4 (S3, mux_4_4_q, ENABLE);
endmodule

module Alu_input_selecter_simplified (
  input  [3:0] R3,
  input  [3:0] R2,
  input  [3:0] R1,
  input  [3:0] R0,
  input  [1:0] Selection,
  input  ENABLE,
  output [3:0] S
);

  wire mux_4_1_q, mux_4_2_q, mux_4_3_q, mux_4_4_q;

  Mux_4 mux_4_1 (.selA(Selection[0]), .selB(Selection[1]), .A(R0[0]), .B(R1[0]), .C(R2[0]), .D(R3[0]), .Q(mux_4_1_q));
  Mux_4 mux_4_2 (.selA(Selection[0]), .selB(Selection[1]), .A(R0[1]), .B(R1[1]), .C(R2[1]), .D(R3[1]), .Q(mux_4_2_q));
  Mux_4 mux_4_3 (.selA(Selection[0]), .selB(Selection[1]), .A(R0[2]), .B(R1[2]), .C(R2[2]), .D(R3[2]), .Q(mux_4_3_q));
  Mux_4 mux_4_4 (.selA(Selection[0]), .selB(Selection[1]), .A(R0[3]), .B(R1[3]), .C(R2[3]), .D(R3[3]), .Q(mux_4_4_q));
  and and_1 (S[0], mux_4_1_q, ENABLE);
  and and_2 (S[1], mux_4_2_q, ENABLE);
  and and_3 (S[2], mux_4_3_q, ENABLE);
  and and_4 (S[3], mux_4_4_q, ENABLE);
endmodule

module Registre_Selection_simplified (
  input  [3:0] Input,
  input  [1:0] R_Selecter,
  input  Master_Reset,
  input  [3:0] Set_R0,
  input  RESET,
  input  [3:0] Set_R1,
  output [3:0] R0,
  output [3:0] R1,
  output [3:0] R2,
  output [3:0] R3
);

  wire demux_1_s0, demux_1_s1, demux_1_s2, demux_1_s3, demux_2_s0, demux_2_s1, demux_2_s2, demux_2_s3,
       demux_3_s0, demux_3_s1, demux_3_s2, demux_3_s3, demux_4_s0, demux_4_s1, demux_4_s2, demux_4_s3,
       demux_5_s0, demux_5_s1, demux_5_s2, demux_5_s3, or_1_out, or_2_out, or_3_out, or_4_out, or_5_out,
       or_6_out, or_7_out, or_8_out, or_9_out, or_10_out, or_11_out, or_12_out;

  DEMUX demux_1 (
    .E(RESET), .SelA(R_Selecter[0]), .SelB(R_Selecter[1]), .S0(demux_1_s0), .S1(demux_1_s1), .S2(demux_1_s2),
    .S3(demux_1_s3));
  DEMUX demux_2 (
    .E(Input[0]), .SelA(R_Selecter[0]), .SelB(R_Selecter[1]), .S0(demux_2_s0), .S1(demux_2_s1),
    .S2(demux_2_s2), .S3(demux_2_s3));
  DEMUX demux_3 (
    .E(Input[1]), .SelA(R_Selecter[0]), .SelB(R_Selecter[1]), .S0(demux_3_s0), .S1(demux_3_s1),
    .S2(demux_3_s2), .S3(demux_3_s3));
  DEMUX demux_4 (
    .E(Input[2]), .SelA(R_Selecter[0]), .SelB(R_Selecter[1]), .S0(demux_4_s0), .S1(demux_4_s1),
    .S2(demux_4_s2), .S3(demux_4_s3));
  DEMUX demux_5 (
    .E(Input[3]), .SelA(R_Selecter[0]), .SelB(R_Selecter[1]), .S0(demux_5_s0), .S1(demux_5_s1),
    .S2(demux_5_s2), .S3(demux_5_s3));
  or or_1 (or_1_out, demux_1_s0, Master_Reset);
  or or_2 (or_2_out, demux_1_s1, Master_Reset);
  or or_3 (or_3_out, demux_1_s2, Master_Reset);
  or or_4 (or_4_out, demux_1_s3, Master_Reset);
  or or_5 (or_5_out, Set_R0[0], demux_2_s0);
  or or_6 (or_6_out, Set_R0[1], demux_3_s0);
  or or_7 (or_7_out, Set_R0[2], demux_4_s0);
  or or_8 (or_8_out, Set_R0[3], demux_5_s0);
  or or_9 (or_9_out, Set_R1[0], demux_2_s1);
  or or_10 (or_10_out, Set_R1[1], demux_3_s1);
  or or_11 (or_11_out, Set_R1[2], demux_4_s1);
  or or_12 (or_12_out, Set_R1[3], demux_5_s1);
  Registre_4_bits registre_4_bits_1 (
    .Reset(or_1_out), .S3(or_8_out), .S2(or_7_out), .S1(or_6_out), .S0(or_5_out), .S0_2(R0[0]), .S1_2(R0[1]),
    .S2_2(R0[2]), .S3_2(R0[3]));
  Registre_4_bits registre_4_bits_2 (
    .Reset(or_2_out), .S3(or_12_out), .S2(or_11_out), .S1(or_10_out), .S0(or_9_out), .S0_2(R1[0]),
    .S1_2(R1[1]), .S2_2(R1[2]), .S3_2(R1[3]));
  Registre_4_bits registre_4_bits_3 (
    .Reset(or_3_out), .S3(demux_5_s2), .S2(demux_4_s2), .S1(demux_3_s2), .S0(demux_2_s2), .S0_2(R2[0]),
    .S1_2(R2[1]), .S2_2(R2[2]), .S3_2(R2[3]));
  Registre_4_bits registre_4_bits_4 (
    .Reset(or_4_out), .S3(demux_5_s3), .S2(demux_4_s3), .S1(demux_3_s3), .S0(demux_2_s3), .S0_2(R3[0]),
    .S1_2(R3[1]), .S2_2(R3[2]), .S3_2(R3[3]));
endmodule

module Alu_4bits_simplified (
  input  [1:0] CTRL,
  input  [3:0] IN_B,
  input  [3:0] IN_A,
  input  Cin,
  input  CLK,
  output [3:0] OUTPUT,
  output [2:0] FLAG_OUT
);

  wire alu_1bit_1_cout, alu_1bit_2_cout, alu_1bit_3_cout, alu_1bit_4_cout;

  Alu_1bit alu_1bit_1 (
    .Cout(alu_1bit_1_cout), .S(OUTPUT[0]), .A(IN_A[0]), .B(IN_B[0]), .Cin(Cin), .Sel_B(CTRL[1]),
    .Sel_A(CTRL[0]));
  Alu_1bit alu_1bit_2 (
    .Cout(alu_1bit_2_cout), .S(OUTPUT[1]), .A(IN_A[1]), .B(IN_B[1]), .Cin(alu_1bit_1_cout), .Sel_B(CTRL[1]),
    .Sel_A(CTRL[0]));
  Alu_1bit alu_1bit_3 (
    .Cout(alu_1bit_3_cout), .S(OUTPUT[2]), .A(IN_A[2]), .B(IN_B[2]), .Cin(alu_1bit_2_cout), .Sel_B(CTRL[1]),
    .Sel_A(CTRL[0]));
  Alu_1bit alu_1bit_4 (
    .Cout(alu_1bit_4_cout), .S(OUTPUT[3]), .A(IN_A[3]), .B(IN_B[3]), .Cin(alu_1bit_3_cout), .Sel_B(CTRL[1]),
    .Sel_A(CTRL[0]));
  flags flags_1 (
    .Alu_Res(OUTPUT), .Cout_In(alu_1bit_4_cout), .Cin_In(Cin), .NULL(FLAG_OUT[0]), .NEGATIF(FLAG_OUT[1]),
    .OVERFLOW(FLAG_OUT[2]), .CLK(CLK));
endmodule

module TEST (
  input  Enable,
  input  [1:0] Sel_A,
  input  [1:0] R_select,
  input  Cin,
  input  [1:0] Select,
  input  [3:0] Input,
  input  [1:0] Sel_B,
  input  [3:0] Set_R1,
  input  [3:0] Set_R0
);

  wire automate_1__0, automate_1__1, automate_1__2, automate_1__3, automate_1__4, automate_1__5,
       automate_1__6, automate_1__7, clock_1_out, Ena_out, L_out, MR_out, or_2_out, or_3_out, or_4_out,
       R_2_out, R_out;
  wire [3:0] alu_4bits_simplified_1_p5, alu_input_selecter_simplified_1_s, alu_input_selecter_simplified_2_s,
       and_1_out, or_1_out, register_4_simplified_1_output, registre_selection_simplified_1_p7,
       registre_selection_simplified_1_p8;
  wire [3:3] or_5_out;

  assign or_1_out = Input | and_1_out;  // OR_Gate or_1, 4 bits wide
  Button R (.out(R_out));
  or or_2 (or_2_out, R_out, automate_1__2);
  Button MR (.out(MR_out));
  // Registre_Selection_simplified registre_selection_simplified_1: pin names not known; wires that end beside it: or_1_out, R_select, Set_R1, MR_out, Set_R0, or_2_out, registre_selection_simplified_1_p7, registre_selection_simplified_1_p8
  Hex_Digit_Display hex_digit_display_1 (.value(registre_selection_simplified_1_p8));  // open: dp
  Hex_Digit_Display hex_digit_display_2 (.value(registre_selection_simplified_1_p7));  // open: dp
  or or_3 (or_3_out, Enable, automate_1__1);
  Alu_input_selecter_simplified alu_input_selecter_simplified_1 (
    .S(alu_input_selecter_simplified_1_s), .R1(registre_selection_simplified_1_p8),
    .R0(registre_selection_simplified_1_p7), .Selection(Sel_A), .ENABLE(or_3_out));  // open: R3, R2
  Alu_input_selecter_simplified alu_input_selecter_simplified_2 (
    .S(alu_input_selecter_simplified_2_s), .R1(registre_selection_simplified_1_p8),
    .R0(registre_selection_simplified_1_p7), .Selection(Sel_B), .ENABLE(or_3_out));  // open: R3, R2
  Hex_Digit_Display hex_digit_display_3 (.value(alu_input_selecter_simplified_2_s));  // open: dp
  Hex_Digit_Display hex_digit_display_4 (.value(alu_input_selecter_simplified_1_s));  // open: dp
  // Alu_4bits_simplified alu_4bits_simplified_1: pin names not known; wires that end beside it: alu_input_selecter_simplified_1_s, alu_input_selecter_simplified_2_s, Cin, Select, alu_4bits_simplified_1_p5
  Hex_Digit_Display hex_digit_display_5 (.value(alu_4bits_simplified_1_p5));  // open: dp
  Button R_2 (.out(R_2_out));
  or or_4 (or_4_out, R_2_out, automate_1__4);
  Register_4_simplified register_4_simplified_1 (
    .Set_4(alu_4bits_simplified_1_p5), .Reset(or_4_out), .Output(register_4_simplified_1_output));
  Hex_Digit_Display hex_digit_display_6 (.value(register_4_simplified_1_output));  // open: dp
  Button Ena (.out(Ena_out));
  or or_5 (or_5_out[3], Ena_out, automate_1__3);
  assign and_1_out = register_4_simplified_1_output & {4{or_5_out[3]}};  // AND_Gate and_1, 4 bits wide
  Button L (.out(L_out));
  Automate automate_1 (
    .CLK(clock_1_out), .Launch(L_out), ._7(automate_1__7), ._6(automate_1__6), ._5(automate_1__5),
    ._4(automate_1__4), ._3(automate_1__3), ._2(automate_1__2), ._1(automate_1__1), ._0(automate_1__0));
  Clock clock_1 (.out(clock_1_out));

  // Notes on the sheet:
  //   Probleme : addition de  2 et 7 : valeur non correct, remise en ordre apres reset
  //   0 : Inactif
  //   1 : ALU IN ENABLE
  //   2 : Reset registre cible
  //   3 : Mise en mémoire ( ENABLE sortie ALU)
  //   4 : Flush (reset memoire tempo et reset automate
  //   Registre temporaire
  //   Launch
endmodule

module Register_4_simplified (
  input  [3:0] Set_4,
  input  Reset,
  output [3:0] Output
);

  RS rs_1 (.S(Set_4[0]), .R(Reset), .Q(Output[0]));
  RS rs_2 (.S(Set_4[1]), .R(Reset), .Q(Output[1]));
  RS rs_3 (.S(Set_4[2]), .R(Reset), .Q(Output[2]));
  RS rs_4 (.S(Set_4[3]), .R(Reset), .Q(Output[3]));
endmodule

module Clocked_register_4 (
  input  [3:0] Set_4,
  input  Reset,
  input  CLK,
  output [3:0] Output
);

  S_R_Flip_Flop s_r_ff_1 (.S(Set_4[0]), .clk(CLK), .R(Reset), .Q(Output[0]));  // open: Qn, preset, reset, en
  S_R_Flip_Flop s_r_ff_2 (.S(Set_4[1]), .clk(CLK), .R(Reset), .Q(Output[1]));  // open: Qn, preset, reset, en
  S_R_Flip_Flop s_r_ff_3 (.S(Set_4[2]), .clk(CLK), .R(Reset), .Q(Output[2]));  // open: Qn, preset, reset, en
  S_R_Flip_Flop s_r_ff_4 (.S(Set_4[3]), .clk(CLK), .R(Reset), .Q(Output[3]));  // open: Qn, preset, reset, en
endmodule

module Alu_input_selecter_simplified_comp (
  input  [3:0] R3,
  input  [3:0] R2,
  input  [3:0] R1,
  input  [3:0] R0,
  input  [1:0] Selection,
  input  Complement,
  input  ENABLE,
  output [3:0] S
);

  wire and_1_out, and_2_out, and_3_out, and_4_out, and_5_out, and_6_out, and_7_out, and_8_out, mux_4_1_q,
       mux_4_2_q, mux_4_3_q, mux_4_4_q, not_1_out, not_2_out, not_3_out, not_4_out, not_5_out, or_1_out,
       or_2_out, or_3_out, or_4_out;

  Mux_4 mux_4_1 (.selA(Selection[0]), .selB(Selection[1]), .A(R0[0]), .B(R1[0]), .C(R2[0]), .D(R3[0]), .Q(mux_4_1_q));
  Mux_4 mux_4_2 (.selA(Selection[0]), .selB(Selection[1]), .A(R0[1]), .B(R1[1]), .C(R2[1]), .D(R3[1]), .Q(mux_4_2_q));
  Mux_4 mux_4_3 (.selA(Selection[0]), .selB(Selection[1]), .A(R0[2]), .B(R1[2]), .C(R2[2]), .D(R3[2]), .Q(mux_4_3_q));
  Mux_4 mux_4_4 (.selA(Selection[0]), .selB(Selection[1]), .A(R0[3]), .B(R1[3]), .C(R2[3]), .D(R3[3]), .Q(mux_4_4_q));
  not not_1 (not_1_out, mux_4_1_q);
  not not_2 (not_2_out, mux_4_2_q);
  not not_3 (not_3_out, mux_4_3_q);
  not not_4 (not_4_out, mux_4_4_q);
  and and_1 (and_1_out, not_4_out, Complement);
  or or_1 (or_1_out, and_1_out, and_2_out);
  not not_5 (not_5_out, Complement);
  and and_2 (and_2_out, mux_4_4_q, not_5_out);
  and and_3 (and_3_out, mux_4_3_q, not_5_out);
  and and_4 (and_4_out, not_3_out, Complement);
  or or_2 (or_2_out, and_4_out, and_3_out);
  and and_5 (and_5_out, not_2_out, Complement);
  and and_6 (and_6_out, mux_4_2_q, not_5_out);
  or or_3 (or_3_out, and_5_out, and_6_out);
  and and_7 (and_7_out, not_1_out, Complement);
  or or_4 (or_4_out, and_7_out, and_8_out);
  and and_8 (and_8_out, mux_4_1_q, not_5_out);
  and and_9 (S[0], or_4_out, ENABLE);
  and and_10 (S[1], or_3_out, ENABLE);
  and and_11 (S[2], or_2_out, ENABLE);
  and and_12 (S[3], or_1_out, ENABLE);
endmodule

module Test2 (
  input  Enable,
  input  [1:0] Sel_A,
  input  [1:0] R_select,
  input  Cin,
  input  [1:0] Select,
  input  [3:0] Input,
  input  [1:0] Sel_B,
  input  [3:0] Set_R1,
  input  [3:0] Set_R0
);

  wire automate_1__0, automate_1__1, automate_1__2, automate_1__3, automate_1__4, automate_1__5,
       automate_1__6, automate_1__7, clock_1_out, Ena_out, L_out, MR_out, or_2_out, or_3_out, or_4_out,
       R_2_out, R_out;
  wire [3:0] alu_4bits_simplified_1_p5, alu_input_selecter_simplified_1_s, alu_input_selecter_simplified_2_s,
       and_1_out, clocked_register_4_1_output, or_1_out, registre_selection_simplified_1_p7,
       registre_selection_simplified_1_p8;
  wire [3:3] or_5_out;

  assign or_1_out = Input | and_1_out;  // OR_Gate or_1, 4 bits wide
  Button R (.out(R_out));
  or or_2 (or_2_out, R_out, automate_1__2);
  Button MR (.out(MR_out));
  // Registre_Selection_simplified registre_selection_simplified_1: pin names not known; wires that end beside it: or_1_out, R_select, Set_R1, MR_out, Set_R0, or_2_out, registre_selection_simplified_1_p7, registre_selection_simplified_1_p8
  Hex_Digit_Display hex_digit_display_1 (.value(registre_selection_simplified_1_p8));  // open: dp
  Hex_Digit_Display hex_digit_display_2 (.value(registre_selection_simplified_1_p7));  // open: dp
  or or_3 (or_3_out, Enable, automate_1__1);
  Alu_input_selecter_simplified alu_input_selecter_simplified_1 (
    .S(alu_input_selecter_simplified_1_s), .R1(registre_selection_simplified_1_p8),
    .R0(registre_selection_simplified_1_p7), .Selection(Sel_A), .ENABLE(or_3_out));  // open: R3, R2
  Alu_input_selecter_simplified alu_input_selecter_simplified_2 (
    .S(alu_input_selecter_simplified_2_s), .R1(registre_selection_simplified_1_p8),
    .R0(registre_selection_simplified_1_p7), .Selection(Sel_B), .ENABLE(or_3_out));  // open: R3, R2
  Hex_Digit_Display hex_digit_display_3 (.value(alu_input_selecter_simplified_2_s));  // open: dp
  Hex_Digit_Display hex_digit_display_4 (.value(alu_input_selecter_simplified_1_s));  // open: dp
  // Alu_4bits_simplified alu_4bits_simplified_1: pin names not known; wires that end beside it: alu_input_selecter_simplified_1_s, alu_input_selecter_simplified_2_s, Cin, Select, alu_4bits_simplified_1_p5
  Hex_Digit_Display hex_digit_display_5 (.value(alu_4bits_simplified_1_p5));  // open: dp
  Button R_2 (.out(R_2_out));
  or or_4 (or_4_out, R_2_out, automate_1__4);
  Clocked_register_4 clocked_register_4_1 (
    .Set_4(alu_4bits_simplified_1_p5), .Output(clocked_register_4_1_output), .Reset(or_4_out),
    .CLK(clock_1_out));
  Hex_Digit_Display hex_digit_display_6 (.value(clocked_register_4_1_output));  // open: dp
  Button Ena (.out(Ena_out));
  or or_5 (or_5_out[3], Ena_out, automate_1__3);
  assign and_1_out = clocked_register_4_1_output & {4{or_5_out[3]}};  // AND_Gate and_1, 4 bits wide
  Button L (.out(L_out));
  Automate automate_1 (
    .CLK(clock_1_out), .Launch(L_out), ._7(automate_1__7), ._6(automate_1__6), ._5(automate_1__5),
    ._4(automate_1__4), ._3(automate_1__3), ._2(automate_1__2), ._1(automate_1__1), ._0(automate_1__0));
  Clock clock_1 (.out(clock_1_out));

  // Notes on the sheet:
  //   0 : Inactif
  //   1 : ALU IN ENABLE
  //   2 : Reset registre cible
  //   3 : Mise en mémoire ( ENABLE sortie ALU)
  //   4 : Flush (reset memoire tempo et reset automate
  //   Registre temporaire
  //   Launch
endmodule

module Register_12 (
  input  [11:0] Rin_12,
  input  CLK,
  input  Reset,
  output [3:0] Operation,
  output [1:0] A,
  output [1:0] Res,
  output [1:0] Ext,
  output [1:0] B
);

  Clocked_register_4 clocked_register_4_1 (.Set_4(Rin_12[11:8]), .Output(Operation), .Reset(Reset), .CLK(CLK));
  Clocked_register_4 clocked_register_4_2 (.Set_4(Rin_12[7:4]), .Output({Res, A}), .Reset(Reset), .CLK(CLK));
  Clocked_register_4 clocked_register_4_3 (.Set_4(Rin_12[3:0]), .Output({B, Ext}), .Reset(Reset), .CLK(CLK));
  Hex_Digit_Display hex_digit_display_1 (.value(Operation));  // open: dp
  Hex_Digit_Display hex_digit_display_2 (.value({Res, A}));  // open: dp
  Hex_Digit_Display hex_digit_display_3 (.value({B, Ext}));  // open: dp
endmodule

module v1 (
  input  Enable,
  input  [1:0] Sel_A,
  input  [1:0] R_select,
  input  [1:0] Select,
  input  [3:0] Input,
  input  [1:0] Sel_B,
  input  [3:0] Set_R1,
  input  [3:0] Set_R0,
  input  Complement
);

  wire automate_1__0, automate_1__1, automate_1__2, automate_1__3, automate_1__4, automate_1__5,
       automate_1__6, automate_1__7, clock_1_out, Ena_out, L_out, MR_out, or_2_out, or_3_out, or_4_out,
       R_2_out, R_out;
  wire [3:0] alu_4bits_simplified_1_p4, and_1_out, clocked_register_4_1_output, or_1_out,
       registre_selection_simplified_1_p7, registre_selection_simplified_1_p8;
  wire [3:1] alu_input_selecter_simplified_1_s;
  wire [3:3] or_5_out;

  assign or_1_out = Input | and_1_out;  // OR_Gate or_1, 4 bits wide
  Button R (.out(R_out));
  or or_2 (or_2_out, R_out, automate_1__2);
  Button MR (.out(MR_out));
  // Registre_Selection_simplified registre_selection_simplified_1: pin names not known; wires that end beside it: or_1_out, R_select, Set_R1, MR_out, Set_R0, or_2_out, registre_selection_simplified_1_p7, registre_selection_simplified_1_p8
  Hex_Digit_Display hex_digit_display_1 (.value(registre_selection_simplified_1_p8));  // open: dp
  Hex_Digit_Display hex_digit_display_2 (.value(registre_selection_simplified_1_p7));  // open: dp
  or or_3 (or_3_out, Enable, automate_1__1);
  Alu_input_selecter_simplified alu_input_selecter_simplified_1 (
    .S({alu_input_selecter_simplified_1_s, Complement}), .R1(registre_selection_simplified_1_p8),
    .R0(registre_selection_simplified_1_p7), .Selection(Sel_A), .ENABLE(or_3_out));  // open: R3, R2
  Alu_input_selecter_simplified_comp alu_input_selecter_simplified_comp_1 (
    .S({alu_input_selecter_simplified_1_s, Complement}), .R1(registre_selection_simplified_1_p8),
    .R0(registre_selection_simplified_1_p7), .Selection(Sel_B), .Complement(Complement), .ENABLE(or_3_out));  // open: R3, R2
  Hex_Digit_Display hex_digit_display_3 (.value({alu_input_selecter_simplified_1_s, Complement}));  // open: dp
  Hex_Digit_Display hex_digit_display_4 (.value({alu_input_selecter_simplified_1_s, Complement}));  // open: dp
  // Alu_4bits_simplified alu_4bits_simplified_1: pin names not known; wires that end beside it: {alu_input_selecter_simplified_1_s, Complement}, {alu_input_selecter_simplified_1_s, Complement}, Select, alu_4bits_simplified_1_p4
  Hex_Digit_Display hex_digit_display_5 (.value(alu_4bits_simplified_1_p4));  // open: dp
  Button R_2 (.out(R_2_out));
  or or_4 (or_4_out, R_2_out, automate_1__4);
  Clocked_register_4 clocked_register_4_1 (
    .Set_4(alu_4bits_simplified_1_p4), .Output(clocked_register_4_1_output), .Reset(or_4_out),
    .CLK(clock_1_out));
  Hex_Digit_Display hex_digit_display_6 (.value(clocked_register_4_1_output));  // open: dp
  Button Ena (.out(Ena_out));
  or or_5 (or_5_out[3], Ena_out, automate_1__3);
  assign and_1_out = clocked_register_4_1_output & {4{or_5_out[3]}};  // AND_Gate and_1, 4 bits wide
  Button L (.out(L_out));
  Automate automate_1 (
    .CLK(clock_1_out), .Launch(L_out), ._7(automate_1__7), ._6(automate_1__6), ._5(automate_1__5),
    ._4(automate_1__4), ._3(automate_1__3), ._2(automate_1__2), ._1(automate_1__1), ._0(automate_1__0));
  Clock clock_1 (.out(clock_1_out));
  // Pins of 1 and 4 bits meet at {alu_input_selecter_simplified_1_s, Complement}

  // Notes on the sheet:
  //   0 : Inactif
  //   1 : ALU IN ENABLE
  //   2 : Reset registre cible
  //   3 : Mise en mémoire ( ENABLE sortie ALU)
  //   4 : Flush (reset memoire tempo et reset automate
  //   Registre temporaire
  //   Launch
endmodule

module V1_1 (
  input  Reset,
  input  [11:0] Ctrl_signal,
  input  Enable,
  input  [3:0] Input,
  input  [3:0] Set_R1,
  input  [3:0] Set_R0,
  input  Complement
);

  wire automate_1__0, automate_1__1, automate_1__2, automate_1__3, automate_1__4, automate_1__5,
       automate_1__6, automate_1__7, clock_1_out, Ena_out, L_out, MR_out, or_2_out, or_3_out, or_4_out,
       or_5_out, R_2_out, R_out;
  wire [1:0] register_12_1_a, register_12_1_b, registre_selection_simplified_1_p2;
  wire [3:0] alu_4bits_simplified_1_p4, and_1_out, and_3_out, clocked_register_4_1_output, or_1_out,
       register_12_1_operation, registre_selection_simplified_1_p6, registre_selection_simplified_1_p7,
       registre_selection_simplified_1_p8;
  wire [3:1] alu_input_selecter_simplified_1_s;
  wire [3:3] Force_set_Memory_out, or_6_out;

  Button R (.out(R_out));
  Button MR (.out(MR_out));
  assign or_1_out = Input | and_3_out;  // OR_Gate or_1, 4 bits wide
  assign and_1_out = Set_R1 & {4{Force_set_Memory_out[3]}};  // AND_Gate and_1, 4 bits wide
  Button Force_set_Memory (.out(Force_set_Memory_out[3]));
  or or_2 (or_2_out, R_out, automate_1__2);
  // Registre_Selection_simplified registre_selection_simplified_1: pin names not known; wires that end beside it: or_1_out, registre_selection_simplified_1_p2, and_1_out, MR_out, or_2_out, registre_selection_simplified_1_p6, registre_selection_simplified_1_p7, registre_selection_simplified_1_p8
  assign registre_selection_simplified_1_p8 = {4{Force_set_Memory_out[3]}} & Set_R0;  // AND_Gate and_2, 4 bits wide
  Hex_Digit_Display hex_digit_display_1 (.value(registre_selection_simplified_1_p7));  // open: dp
  Hex_Digit_Display hex_digit_display_2 (.value(registre_selection_simplified_1_p6));  // open: dp
  or or_3 (or_3_out, Enable, automate_1__1);
  Alu_input_selecter_simplified alu_input_selecter_simplified_1 (
    .S({alu_input_selecter_simplified_1_s, Complement}), .R1(registre_selection_simplified_1_p7),
    .R0(registre_selection_simplified_1_p6), .Selection(register_12_1_a), .ENABLE(or_3_out));  // open: R3, R2
  Alu_input_selecter_simplified_comp alu_input_selecter_simplified_comp_1 (
    .S({alu_input_selecter_simplified_1_s, Complement}), .R1(registre_selection_simplified_1_p7),
    .R0(registre_selection_simplified_1_p6), .Selection(register_12_1_b), .Complement(Complement),
    .ENABLE(or_3_out));  // open: R3, R2
  Hex_Digit_Display hex_digit_display_3 (.value({alu_input_selecter_simplified_1_s, Complement}));  // open: dp
  Hex_Digit_Display hex_digit_display_4 (.value({alu_input_selecter_simplified_1_s, Complement}));  // open: dp
  Register_12 register_12_1 (
    .Rin_12(Ctrl_signal), .Operation(register_12_1_operation), .A(register_12_1_a),
    .Res(registre_selection_simplified_1_p2), .B(register_12_1_b), .Reset(or_4_out), .CLK(clock_1_out));  // open: Ext
  // Alu_4bits_simplified alu_4bits_simplified_1: pin names not known; wires that end beside it: {alu_input_selecter_simplified_1_s, Complement}, {alu_input_selecter_simplified_1_s, Complement}, register_12_1_operation[1:0], alu_4bits_simplified_1_p4
  or or_4 (or_4_out, Reset, automate_1__4);
  Hex_Digit_Display hex_digit_display_5 (.value(alu_4bits_simplified_1_p4));  // open: dp
  Button R_2 (.out(R_2_out));
  or or_5 (or_5_out, R_2_out, automate_1__4);
  Hex_Digit_Display hex_digit_display_6 (.value(clocked_register_4_1_output));  // open: dp
  Clocked_register_4 clocked_register_4_1 (
    .Set_4(alu_4bits_simplified_1_p4), .Output(clocked_register_4_1_output), .Reset(or_5_out),
    .CLK(clock_1_out));
  Button Ena (.out(Ena_out));
  assign and_3_out = clocked_register_4_1_output & {4{or_6_out[3]}};  // AND_Gate and_3, 4 bits wide
  or or_6 (or_6_out[3], Ena_out, automate_1__3);
  Button L (.out(L_out));
  Clock clock_1 (.out(clock_1_out));
  Automate automate_1 (
    .CLK(clock_1_out), .Launch(L_out), ._7(automate_1__7), ._6(automate_1__6), ._5(automate_1__5),
    ._4(automate_1__4), ._3(automate_1__3), ._2(automate_1__2), ._1(automate_1__1), ._0(automate_1__0));
  // Pins of 1 and 4 bits meet at {alu_input_selecter_simplified_1_s, Complement}

  // Notes on the sheet:
  //   Registre temporaire
  //   Launch
  //   0 : Inactif
  //   1 : ALU IN ENABLE
  //   2 : Reset registre cible
  //   3 : Mise en mémoire ( ENABLE sortie ALU)
  //   4 : Flush (reset memoire tempo et reset automate
endmodule

module Test_Ram (
  input  [3:0] Data_in,
  input  Write,
  input  [5:0] Outpin,
  input  Reset_writing_state,
  input  CLK,
  output [3:0] Data_out
);

  wire not_1_out, rs_1_q;

  RS rs_1 (.S(Write), .R(Reset_writing_state), .Q(rs_1_q));
  assign Data_out = rs_1_q ? Data_in : 4'bz;  // Controlled_Buffer controlled_buffer_1
  not not_1 (not_1_out, rs_1_q);
  RAM #(.addrWidth(6), .dataWidth(4)) ram_1 (
    .addr(Outpin), .data(Data_out), .clk(CLK), .ld(not_1_out));  // open: sel, clr

  // Notes on the sheet:
  //   Ne pas oublier de reset cette bascule a chaque premier lancement
endmodule

module Ram (
  input  [3:0] Data_in,
  input  Write,
  input  [5:0] Address,
  input  Reset_writing_state,
  input  CLK,
  input  Enable_output,
  output [3:0] Data_out
);

  wire not_1_out, rs_1_q;
  wire [3:0] controlled_buffer_1_out;

  RS rs_1 (.S(Write), .R(Reset_writing_state), .Q(rs_1_q));
  assign controlled_buffer_1_out = rs_1_q ? Data_in : 4'bz;  // Controlled_Buffer controlled_buffer_1
  not not_1 (not_1_out, rs_1_q);
  RAM #(.addrWidth(6), .dataWidth(4)) ram_1 (
    .addr(Address), .data(controlled_buffer_1_out), .clk(CLK), .ld(not_1_out));  // open: sel, clr
  assign Data_out = controlled_buffer_1_out & {4{Enable_output}};  // AND_Gate and_1, 4 bits wide

  // Notes on the sheet:
  //   Ne pas oublier de reset cette bascule a chaque premier lancement
endmodule

module Automate_ctrl_Entry (
  input  CLK,
  input  Launch,
  input  [1:0] EXT_JUMP_CTRL,
  input  [1:0] Ctrl_IN,
  input  [2:0] FLAG_IN,
  output Alu_Enable,
  output Reset_registre_cible,
  output Enable_Sortie_Alu,
  output Ram_Write,
  output Enable_Ram_Output,
  output FLUSH,
  output PC_Write_External
);

  wire and_1_out, and_2_out, and_3_out, and_4_out, and_5_out, and_6_out, and_7_out, and_8_out, and_9_out,
       d_ff_1_q, d_ff_1_qn, d_ff_2_q, d_ff_2_qn, d_ff_3_q, d_ff_3_qn, decodeur_8_1_s0, decodeur_8_1_s1,
       decodeur_8_1_s2, decodeur_8_1_s3, decodeur_8_1_s4, decodeur_8_1_s5, decodeur_8_1_s6,
       multiplexer_1_out, not_1_out, not_2_out, not_3_out, not_4_out, not_5_out, not_6_out, not_7_out,
       not_8_out, not_9_out, not_10_out, not_11_out, not_12_out, or_1_out, or_2_out, rs_1_q;

  RS rs_1 (.S(Launch), .R(FLUSH), .Q(rs_1_q));
  and and_1 (and_1_out, CLK, rs_1_q);
  not not_1 (not_1_out, not_2_out);
  not not_2 (not_2_out, CLK);
  not not_3 (not_3_out, not_1_out);
  not not_4 (not_4_out, not_3_out);
  not not_5 (not_5_out, d_ff_1_q);
  not not_6 (not_6_out, d_ff_2_q);
  not not_7 (not_7_out, d_ff_1_q);
  not not_8 (not_8_out, d_ff_1_q);
  not not_9 (not_9_out, d_ff_2_q);
  not not_10 (not_10_out, d_ff_3_q);
  and and_2 (and_2_out, not_5_out, and_1_out);
  and and_3 (and_3_out, d_ff_1_q, not_6_out);
  and and_4 (and_4_out, not_7_out, d_ff_2_q);
  and and_5 (and_5_out, not_8_out, d_ff_3_q);
  and and_6 (and_6_out, not_9_out, d_ff_3_q);
  and and_7 (and_7_out, d_ff_1_q, d_ff_2_q, not_10_out);
  or or_1 (or_1_out, and_3_out, and_4_out);
  or or_2 (or_2_out, and_5_out, and_6_out, and_7_out);
  and and_8 (and_8_out, or_1_out, and_1_out);
  and and_9 (and_9_out, or_2_out, and_1_out);
  Multiplexer #(.select(2)) multiplexer_1 (
    .in0(1'b1), .in1(FLAG_IN[0]), .in2(FLAG_IN[1]), .in3(FLAG_IN[2]), .out(multiplexer_1_out),
    .sel(EXT_JUMP_CTRL));  // open: en
  not not_11 (not_11_out, Ctrl_IN[0]);
  not not_12 (not_12_out, Ctrl_IN[1]);
  D_Flip_Flop d_ff_1 (.clk(not_4_out), .D(and_2_out), .Q(d_ff_1_q), .Qn(d_ff_1_qn));  // open: preset, en, reset
  D_Flip_Flop d_ff_2 (.clk(not_4_out), .D(and_8_out), .Q(d_ff_2_q), .Qn(d_ff_2_qn));  // open: preset, en, reset
  D_Flip_Flop d_ff_3 (.clk(not_4_out), .D(and_9_out), .Q(d_ff_3_q), .Qn(d_ff_3_qn));  // open: preset, en, reset
  Decodeur_8 decodeur_8_1 (
    .S0(decodeur_8_1_s0), .S1(decodeur_8_1_s1), .S2(decodeur_8_1_s2), .S3(decodeur_8_1_s3),
    .S4(decodeur_8_1_s4), .S5(decodeur_8_1_s5), .S6(decodeur_8_1_s6), .S7(FLUSH), .Sel2(d_ff_3_q),
    .Sel1(d_ff_2_q), .Sel0(d_ff_1_q));
  and and_10 (Alu_Enable, decodeur_8_1_s1, not_11_out, not_12_out);
  and and_11 (Reset_registre_cible, decodeur_8_1_s2, not_12_out);
  and and_12 (Enable_Sortie_Alu, decodeur_8_1_s3, not_11_out, not_12_out);
  and and_13 (Ram_Write, decodeur_8_1_s1, Ctrl_IN[1], not_11_out);
  and and_14 (Enable_Ram_Output, decodeur_8_1_s3, Ctrl_IN[0], not_12_out);
  and and_15 (PC_Write_External, FLUSH, Ctrl_IN[0], Ctrl_IN[1], multiplexer_1_out);

  // Notes on the sheet:
  //   Uilisé pour créer un delay (Bascule D réglées en rising edge pour eviter toute oscillation
  //   Control bits : 00XX
  //   0 : Inactif
  //   1 : ALU IN ENABLE
  //   2 : Reset registre cible
  //   Control bits : 10XX Store
  //   0 : Inactif
  //   1 : Write = 1
  //   7 : Flush
  //   Control bits : 01XX Load
  //   0 : Inactif
  //   7 : Flush
  //   Control bits : 11XX Jump
  //   0 : Inactif
  //   3 : Mise en mémoire ( ENABLE sortie ALU)
  //   7 : Flush (reset memoire tempo et reset automate
  //   2 : Reset registre cible
  //   3 : Mise en mémoire ( ENABLE sortie RAM)
  //   7 : Flush + PC Write External
endmodule

module V1_2 (
  input  Reset,
  input  [11:0] Ctrl_signal,
  input  Outpin,
  input  Enable,
  input  [3:0] Input,
  input  [3:0] Set_R1,
  input  [3:0] Set_R0,
  input  Complement,
  output [5:0] out_9
);

  wire automate_1__0, automate_1__1, automate_1__2, automate_1__3, automate_1__4, automate_1__5,
       automate_1__6, automate_1__7, clock_1_out, Ena_out, L_out, MR_out, or_2_out, or_3_out, or_4_out,
       or_5_out, R_2_out, R_out;
  wire [1:0] registre_selection_simplified_1_p2;
  wire [3:0] alu_4bits_simplified_1_p4, alu_input_selecter_simplified_1_s, and_1_out, and_3_out,
       clocked_register_4_1_output, or_1_out, ram_1_data_out, register_12_1_operation,
       registre_selection_simplified_1_p6, registre_selection_simplified_1_p7,
       registre_selection_simplified_1_p8;
  wire [3:1] alu_input_selecter_simplified_2_s;
  wire [3:3] Force_set_Memory_out, or_6_out;

  Alu_input_selecter_simplified alu_input_selecter_simplified_1 (
    .S(alu_input_selecter_simplified_1_s), .R1(registre_selection_simplified_1_p7),
    .R0(registre_selection_simplified_1_p6), .Selection(registre_selection_simplified_1_p2));  // open: R3, R2, ENABLE
  Button R (.out(R_out));
  Button MR (.out(MR_out));
  assign or_1_out = ram_1_data_out | Input | and_3_out;  // OR_Gate or_1, 4 bits wide
  assign and_1_out = Set_R1 & {4{Force_set_Memory_out[3]}};  // AND_Gate and_1, 4 bits wide
  Button Force_set_Memory (.out(Force_set_Memory_out[3]));
  or or_2 (or_2_out, R_out, automate_1__2);
  // Registre_Selection_simplified registre_selection_simplified_1: pin names not known; wires that end beside it: or_1_out, registre_selection_simplified_1_p2, and_1_out, MR_out, or_2_out, registre_selection_simplified_1_p6, registre_selection_simplified_1_p7, registre_selection_simplified_1_p8
  assign registre_selection_simplified_1_p8 = {4{Force_set_Memory_out[3]}} & Set_R0;  // AND_Gate and_2, 4 bits wide
  Ram ram_1 (
    .Data_in(alu_input_selecter_simplified_1_s), .Write(register_12_1_operation[3]), .Address(out_9),
    .Reset_writing_state(MR_out), .Data_out(ram_1_data_out), .CLK(clock_1_out), .Enable_output(Outpin));
  Hex_Digit_Display hex_digit_display_1 (.value(registre_selection_simplified_1_p7));  // open: dp
  Hex_Digit_Display hex_digit_display_2 (.value(registre_selection_simplified_1_p6));  // open: dp
  or or_3 (or_3_out, Enable, automate_1__1);
  Alu_input_selecter_simplified alu_input_selecter_simplified_2 (
    .S({alu_input_selecter_simplified_2_s, Complement}), .R1(registre_selection_simplified_1_p7),
    .R0(registre_selection_simplified_1_p6), .Selection(out_9[5:4]), .ENABLE(or_3_out));  // open: R3, R2
  Alu_input_selecter_simplified_comp alu_input_selecter_simplified_comp_1 (
    .S({alu_input_selecter_simplified_2_s, Complement}), .R1(registre_selection_simplified_1_p7),
    .R0(registre_selection_simplified_1_p6), .Selection(out_9[3:2]), .Complement(Complement),
    .ENABLE(or_3_out));  // open: R3, R2
  Hex_Digit_Display hex_digit_display_3 (.value({alu_input_selecter_simplified_2_s, Complement}));  // open: dp
  Hex_Digit_Display hex_digit_display_4 (.value({alu_input_selecter_simplified_2_s, Complement}));  // open: dp
  Register_12 register_12_1 (
    .Rin_12(Ctrl_signal), .Operation(register_12_1_operation), .A(out_9[5:4]),
    .Res(registre_selection_simplified_1_p2), .Ext(out_9[1:0]), .B(out_9[3:2]), .Reset(or_4_out),
    .CLK(clock_1_out));
  // Alu_4bits_simplified alu_4bits_simplified_1: pin names not known; wires that end beside it: {alu_input_selecter_simplified_2_s, Complement}, {alu_input_selecter_simplified_2_s, Complement}, register_12_1_operation[1:0], alu_4bits_simplified_1_p4
  or or_4 (or_4_out, Reset, automate_1__4);
  Hex_Digit_Display hex_digit_display_5 (.value(alu_4bits_simplified_1_p4));  // open: dp
  Button R_2 (.out(R_2_out));
  or or_5 (or_5_out, R_2_out, automate_1__4);
  Hex_Digit_Display hex_digit_display_6 (.value(clocked_register_4_1_output));  // open: dp
  Clocked_register_4 clocked_register_4_1 (
    .Set_4(alu_4bits_simplified_1_p4), .Output(clocked_register_4_1_output), .Reset(or_5_out),
    .CLK(clock_1_out));
  Button Ena (.out(Ena_out));
  assign and_3_out = clocked_register_4_1_output & {4{or_6_out[3]}};  // AND_Gate and_3, 4 bits wide
  or or_6 (or_6_out[3], Ena_out, automate_1__3);
  Button L (.out(L_out));
  Clock clock_1 (.out(clock_1_out));
  Automate automate_1 (
    .CLK(clock_1_out), .Launch(L_out), ._7(automate_1__7), ._6(automate_1__6), ._5(automate_1__5),
    ._4(automate_1__4), ._3(automate_1__3), ._2(automate_1__2), ._1(automate_1__1), ._0(automate_1__0));
  // Pins of 1 and 4 bits meet at {alu_input_selecter_simplified_2_s, Complement}

  // Notes on the sheet:
  //   Utilisé comme Mux 4
  //   Visualisation IMM
  //   Registre temporaire
  //   Launch
  //   0 : Inactif
  //   1 : ALU IN ENABLE
  //   2 : Reset registre cible
  //   3 : Mise en mémoire ( ENABLE sortie ALU)
  //   4 : Flush (reset memoire tempo et reset automate
endmodule

module Register4_W_R (
  input  CLK,
  input  [3:0] IN,
  input  Write,
  input  Read,
  output [3:0] OUT
);

  Register1_W_R register1_w_r_1 (.Outpin(CLK), .out_5(OUT[0]), .In(IN[0]), .Write(Write), .Read(Read));
  Register1_W_R register1_w_r_2 (.Outpin(CLK), .out_5(OUT[1]), .In(IN[1]), .Write(Write), .Read(Read));
  Register1_W_R register1_w_r_3 (.Outpin(CLK), .out_5(OUT[2]), .In(IN[2]), .Write(Write), .Read(Read));
  Register1_W_R register1_w_r_4 (.Outpin(CLK), .out_5(OUT[3]), .In(IN[3]), .Write(Write), .Read(Read));
endmodule

module Register1_W_R (
  input  Outpin,
  input  In,
  input  Write,
  input  Read,
  output out_5
);

  wire controlled_buffer_1_out, d_ff_1_q;

  assign controlled_buffer_1_out = Write ? In : 1'bz;  // Controlled_Buffer controlled_buffer_1
  D_Flip_Flop d_ff_1 (.clk(Outpin), .D(controlled_buffer_1_out), .Q(d_ff_1_q));  // open: Qn, preset, en, reset
  assign out_5 = Read ? d_ff_1_q : 1'bz;  // Controlled_Buffer controlled_buffer_2
endmodule

module Incrementer (
  input  [3:0] Inc_IN,
  output [3:0] Inc_OUT,
  output Cout
);

  wire full_adder_1_cout, full_adder_2_cout, full_adder_3_cout, not_1_out;

  not not_1 (not_1_out, 1'b1);
  Full_adder full_adder_1 (.A(Inc_IN[0]), .B(not_1_out), .Cin(1'b1), .S(Inc_OUT[0]), .Cout(full_adder_1_cout));
  Full_adder full_adder_2 (
    .A(Inc_IN[1]), .B(not_1_out), .Cin(full_adder_1_cout), .S(Inc_OUT[1]), .Cout(full_adder_2_cout));
  Full_adder full_adder_3 (
    .A(Inc_IN[2]), .B(not_1_out), .Cin(full_adder_2_cout), .S(Inc_OUT[2]), .Cout(full_adder_3_cout));
  Full_adder full_adder_4 (.A(Inc_IN[3]), .B(not_1_out), .Cin(full_adder_3_cout), .S(Inc_OUT[3]), .Cout(Cout));
endmodule

module Inc_Registre (
  input  Outpin,
  output Cout,
  output [3:0] PC_Count
);

  wire and_1_out, not_1_out;
  wire [3:0] incrementer_1_inc_out;

  Hex_Digit_Display hex_digit_display_1 (.value(PC_Count));  // open: dp
  Register4_W_R register4_w_r_1 (
    .IN(incrementer_1_inc_out), .OUT(PC_Count), .CLK(Outpin), .Write(and_1_out), .Read(1'b1));
  and and_1 (and_1_out, not_1_out, 1'b1);
  Hex_Digit_Display hex_digit_display_2 (.value(incrementer_1_inc_out));  // open: dp
  Incrementer incrementer_1 (.Inc_IN(PC_Count), .Inc_OUT(incrementer_1_inc_out), .Cout(Cout));
  not not_1 (not_1_out, Cout);
endmodule

module V1_3 (
  input  Reset,
  input  [11:0] Ctrl_signal,
  input  Enable,
  input  [3:0] Input,
  input  [3:0] Set_R1,
  input  [3:0] Set_R0,
  input  Complement,
  output [5:0] out_8
);

  wire automate_ctrl_entry_1_p2, automate_ctrl_entry_1_p3, automate_ctrl_entry_1_p5,
       automate_ctrl_entry_1_p6, automate_ctrl_entry_1_p8, automate_ctrl_entry_1_p9, clock_1_out, Ena_out,
       L_out, MR_out, or_2_out, or_3_out, or_4_out, or_5_out, or_6_out, R_2_out, R_out;
  wire [1:0] registre_selection_simplified_1_p2;
  wire [3:0] alu_4bits_simplified_1_p4, alu_input_selecter_simplified_1_s, and_1_out, and_3_out,
       clocked_register_4_1_output, or_1_out, ram_1_data_out, register_12_1_operation,
       registre_selection_simplified_1_p6, registre_selection_simplified_1_p7,
       registre_selection_simplified_1_p8;
  wire [3:1] alu_input_selecter_simplified_2_s;
  wire [3:3] Force_set_Memory_out, or_7_out;

  Alu_input_selecter_simplified alu_input_selecter_simplified_1 (
    .S(alu_input_selecter_simplified_1_s), .R1(registre_selection_simplified_1_p7),
    .R0(registre_selection_simplified_1_p6), .Selection(registre_selection_simplified_1_p2), .ENABLE(1'b1));  // open: R3, R2
  Button R (.out(R_out));
  Button MR (.out(MR_out));
  assign or_1_out = ram_1_data_out | Input | and_3_out;  // OR_Gate or_1, 4 bits wide
  assign and_1_out = Set_R1 & {4{Force_set_Memory_out[3]}};  // AND_Gate and_1, 4 bits wide
  Button Force_set_Memory (.out(Force_set_Memory_out[3]));
  or or_2 (or_2_out, MR_out, automate_ctrl_entry_1_p2);
  or or_3 (or_3_out, R_out, automate_ctrl_entry_1_p8);
  // Registre_Selection_simplified registre_selection_simplified_1: pin names not known; wires that end beside it: or_1_out, registre_selection_simplified_1_p2, and_1_out, MR_out, or_3_out, registre_selection_simplified_1_p6, registre_selection_simplified_1_p7, registre_selection_simplified_1_p8
  assign registre_selection_simplified_1_p8 = {4{Force_set_Memory_out[3]}} & Set_R0;  // AND_Gate and_2, 4 bits wide
  Ram ram_1 (
    .Data_in(alu_input_selecter_simplified_1_s), .Write(automate_ctrl_entry_1_p5), .Address(out_8),
    .Reset_writing_state(or_2_out), .Data_out(ram_1_data_out), .CLK(clock_1_out),
    .Enable_output(automate_ctrl_entry_1_p3));
  Hex_Digit_Display hex_digit_display_1 (.value(registre_selection_simplified_1_p7));  // open: dp
  Hex_Digit_Display hex_digit_display_2 (.value(registre_selection_simplified_1_p6));  // open: dp
  or or_4 (or_4_out, Enable, automate_ctrl_entry_1_p9);
  Alu_input_selecter_simplified alu_input_selecter_simplified_2 (
    .S({alu_input_selecter_simplified_2_s, Complement}), .R1(registre_selection_simplified_1_p7),
    .R0(registre_selection_simplified_1_p6), .Selection(out_8[5:4]), .ENABLE(or_4_out));  // open: R3, R2
  Alu_input_selecter_simplified_comp alu_input_selecter_simplified_comp_1 (
    .S({alu_input_selecter_simplified_2_s, Complement}), .R1(registre_selection_simplified_1_p7),
    .R0(registre_selection_simplified_1_p6), .Selection(out_8[3:2]), .Complement(Complement),
    .ENABLE(or_4_out));  // open: R3, R2
  Hex_Digit_Display hex_digit_display_3 (.value({alu_input_selecter_simplified_2_s, Complement}));  // open: dp
  Hex_Digit_Display hex_digit_display_4 (.value({alu_input_selecter_simplified_2_s, Complement}));  // open: dp
  Register_12 register_12_1 (
    .Rin_12(Ctrl_signal), .Operation(register_12_1_operation), .A(out_8[5:4]),
    .Res(registre_selection_simplified_1_p2), .Ext(out_8[1:0]), .B(out_8[3:2]), .Reset(or_5_out),
    .CLK(clock_1_out));
  // Alu_4bits_simplified alu_4bits_simplified_1: pin names not known; wires that end beside it: {alu_input_selecter_simplified_2_s, Complement}, {alu_input_selecter_simplified_2_s, Complement}, register_12_1_operation[1:0], alu_4bits_simplified_1_p4
  or or_5 (or_5_out, Reset, automate_ctrl_entry_1_p2);
  Hex_Digit_Display hex_digit_display_5 (.value(alu_4bits_simplified_1_p4));  // open: dp
  Button R_2 (.out(R_2_out));
  or or_6 (or_6_out, R_2_out, automate_ctrl_entry_1_p2);
  Hex_Digit_Display hex_digit_display_6 (.value(clocked_register_4_1_output));  // open: dp
  Clocked_register_4 clocked_register_4_1 (
    .Set_4(alu_4bits_simplified_1_p4), .Output(clocked_register_4_1_output), .Reset(or_6_out),
    .CLK(clock_1_out));
  Button Ena (.out(Ena_out));
  assign and_3_out = clocked_register_4_1_output & {4{or_7_out[3]}};  // AND_Gate and_3, 4 bits wide
  Clock clock_1 (.out(clock_1_out));
  or or_7 (or_7_out[3], Ena_out, automate_ctrl_entry_1_p6);
  Button L (.out(L_out));
  // Automate_ctrl_Entry automate_ctrl_entry_1: pin names not known; wires that end beside it: L_out, automate_ctrl_entry_1_p2, automate_ctrl_entry_1_p3, clock_1_out, automate_ctrl_entry_1_p5, automate_ctrl_entry_1_p6, register_12_1_operation[3:2], automate_ctrl_entry_1_p8, automate_ctrl_entry_1_p9
  // Pins of 1 and 4 bits meet at {alu_input_selecter_simplified_2_s, Complement}

  // Notes on the sheet:
  //   Utilisé comme Mux 4
  //   Visualisation IMM
  //   Registre temporaire
  //   Launch
  //   0 : Inactif
  //   1 : ALU IN ENABLE
  //   2 : Reset registre cible
  //   3 : Mise en mémoire ( ENABLE sortie ALU)
  //   4 : Flush (reset memoire tempo et reset automate
endmodule

module CTRL_V2 (
  input  [11:0] Rin_12,
  output [3:0] Operation,
  output [1:0] A,
  output [1:0] Res,
  output [1:0] Ext,
  output [1:0] B
);

  Hex_Digit_Display hex_digit_display_1 (.value(Rin_12[11:8]));  // open: dp
  Hex_Digit_Display hex_digit_display_2 (.value(Rin_12[7:4]));  // open: dp
  Hex_Digit_Display hex_digit_display_3 (.value(Rin_12[3:0]));  // open: dp

  assign A = Rin_12[5:4];
  assign B = Rin_12[3:2];
  assign Ext = Rin_12[1:0];
  assign Operation = Rin_12[11:8];
  assign Res = Rin_12[7:6];
endmodule

module V1_4 (
  input  [11:0] Ctrl_signal,
  input  Enable,
  input  [3:0] Input,
  input  [3:0] Set_R1,
  input  [3:0] Set_R0,
  input  Complement,
  output [5:0] out_7
);

  wire automate_ctrl_entry_1_p2, automate_ctrl_entry_1_p3, automate_ctrl_entry_1_p5,
       automate_ctrl_entry_1_p6, automate_ctrl_entry_1_p8, automate_ctrl_entry_1_p9, clock_1_out, Ena_out,
       L_out, MR_out, or_2_out, or_3_out, or_4_out, or_5_out, R_2_out, R_out;
  wire [1:0] registre_selection_simplified_1_p2;
  wire [3:0] alu_4bits_simplified_1_p4, alu_input_selecter_simplified_1_s, and_3_out,
       clocked_register_4_1_output, ctrl_v2_1_operation, or_1_out, ram_1_data_out,
       registre_selection_simplified_1_p3, registre_selection_simplified_1_p6,
       registre_selection_simplified_1_p7, registre_selection_simplified_1_p8;
  wire [3:1] alu_input_selecter_simplified_2_s;
  wire [3:3] Force_set_Memory_out, or_6_out;

  Alu_input_selecter_simplified alu_input_selecter_simplified_1 (
    .S(alu_input_selecter_simplified_1_s), .R1(registre_selection_simplified_1_p7),
    .R0(registre_selection_simplified_1_p6), .Selection(registre_selection_simplified_1_p2), .ENABLE(1'b1));  // open: R3, R2
  assign or_1_out = ram_1_data_out | Input | and_3_out;  // OR_Gate or_1, 4 bits wide
  Button R (.out(R_out));
  or or_2 (or_2_out, R_out, automate_ctrl_entry_1_p8);
  Button MR (.out(MR_out));
  // Registre_Selection_simplified registre_selection_simplified_1: pin names not known; wires that end beside it: or_1_out, registre_selection_simplified_1_p2, registre_selection_simplified_1_p3, MR_out, or_2_out, registre_selection_simplified_1_p6, registre_selection_simplified_1_p7, registre_selection_simplified_1_p8
  assign registre_selection_simplified_1_p8 = {4{Force_set_Memory_out[3]}} & Set_R0;  // AND_Gate and_1, 4 bits wide
  assign registre_selection_simplified_1_p3 = Set_R1 & {4{Force_set_Memory_out[3]}};  // AND_Gate and_2, 4 bits wide
  Button Force_set_Memory (.out(Force_set_Memory_out[3]));
  or or_3 (or_3_out, MR_out, automate_ctrl_entry_1_p2);
  Ram ram_1 (
    .Data_in(alu_input_selecter_simplified_1_s), .Write(automate_ctrl_entry_1_p5), .Address(out_7),
    .Reset_writing_state(or_3_out), .Data_out(ram_1_data_out), .CLK(clock_1_out),
    .Enable_output(automate_ctrl_entry_1_p3));
  Hex_Digit_Display hex_digit_display_1 (.value(registre_selection_simplified_1_p7));  // open: dp
  Hex_Digit_Display hex_digit_display_2 (.value(registre_selection_simplified_1_p6));  // open: dp
  or or_4 (or_4_out, Enable, automate_ctrl_entry_1_p9);
  Alu_input_selecter_simplified alu_input_selecter_simplified_2 (
    .S({alu_input_selecter_simplified_2_s, Complement}), .R1(registre_selection_simplified_1_p7),
    .R0(registre_selection_simplified_1_p6), .Selection(out_7[5:4]), .ENABLE(or_4_out));  // open: R3, R2
  Alu_input_selecter_simplified_comp alu_input_selecter_simplified_comp_1 (
    .S({alu_input_selecter_simplified_2_s, Complement}), .R1(registre_selection_simplified_1_p7),
    .R0(registre_selection_simplified_1_p6), .Selection(out_7[3:2]), .Complement(Complement),
    .ENABLE(or_4_out));  // open: R3, R2
  Hex_Digit_Display hex_digit_display_3 (.value({alu_input_selecter_simplified_2_s, Complement}));  // open: dp
  CTRL_V2 ctrl_v2_1 (
    .Rin_12(Ctrl_signal), .Operation(ctrl_v2_1_operation), .A(out_7[5:4]),
    .Res(registre_selection_simplified_1_p2), .Ext(out_7[1:0]), .B(out_7[3:2]));
  Hex_Digit_Display hex_digit_display_4 (.value({alu_input_selecter_simplified_2_s, Complement}));  // open: dp
  // Alu_4bits_simplified alu_4bits_simplified_1: pin names not known; wires that end beside it: {alu_input_selecter_simplified_2_s, Complement}, {alu_input_selecter_simplified_2_s, Complement}, ctrl_v2_1_operation[1:0], alu_4bits_simplified_1_p4
  Button R_2 (.out(R_2_out));
  or or_5 (or_5_out, R_2_out, automate_ctrl_entry_1_p2);
  Hex_Digit_Display hex_digit_display_5 (.value(alu_4bits_simplified_1_p4));  // open: dp
  Hex_Digit_Display hex_digit_display_6 (.value(clocked_register_4_1_output));  // open: dp
  Clocked_register_4 clocked_register_4_1 (
    .Set_4(alu_4bits_simplified_1_p4), .Output(clocked_register_4_1_output), .Reset(or_5_out),
    .CLK(clock_1_out));
  Button Ena (.out(Ena_out));
  or or_6 (or_6_out[3], Ena_out, automate_ctrl_entry_1_p6);
  assign and_3_out = clocked_register_4_1_output & {4{or_6_out[3]}};  // AND_Gate and_3, 4 bits wide
  Clock clock_1 (.out(clock_1_out));
  Button L (.out(L_out));
  // Automate_ctrl_Entry automate_ctrl_entry_1: pin names not known; wires that end beside it: L_out, automate_ctrl_entry_1_p2, automate_ctrl_entry_1_p3, clock_1_out, automate_ctrl_entry_1_p5, automate_ctrl_entry_1_p6, ctrl_v2_1_operation[3:2], automate_ctrl_entry_1_p8, automate_ctrl_entry_1_p9
  // Pins of 1 and 4 bits meet at {alu_input_selecter_simplified_2_s, Complement}

  // Notes on the sheet:
  //   Utilisé comme Mux 4
  //   Visualisation IMM
  //   Registre temporaire
  //   Launch
  //   0 : Inactif
  //   1 : ALU IN ENABLE
  //   2 : Reset registre cible
  //   3 : Mise en mémoire ( ENABLE sortie ALU)
  //   4 : Flush (reset memoire tempo et reset automate
endmodule

module Inc_Registre_Ext (
  input  CLK,
  input  External_Write,
  input  [3:0] External_line_input,
  output Cout,
  output [3:0] PC_Count
);

  wire not_1_out, not_2_out, not_3_out, not_4_out, not_5_out, not_6_out, or_1_out;
  wire [3:0] controlled_buffer_1_out, incrementer_1_inc_out;

  assign controlled_buffer_1_out = External_Write ? External_line_input : 4'bz;  // Controlled_Buffer controlled_buffer_1
  not not_1 (not_1_out, CLK);
  not not_2 (not_2_out, not_1_out);
  not not_3 (not_3_out, not_2_out);
  not not_4 (not_4_out, External_Write);
  not not_5 (not_5_out, not_3_out);
  assign controlled_buffer_1_out = not_4_out ? incrementer_1_inc_out : 4'bz;  // Controlled_Buffer controlled_buffer_2
  Hex_Digit_Display hex_digit_display_1 (.value(PC_Count));  // open: dp
  Register4_W_R register4_w_r_1 (
    .IN(controlled_buffer_1_out), .OUT(PC_Count), .CLK(not_5_out), .Write(or_1_out), .Read(1'b1));
  or or_1 (or_1_out, not_6_out, External_Write);
  Hex_Digit_Display hex_digit_display_2 (.value(incrementer_1_inc_out));  // open: dp
  Incrementer incrementer_1 (.Inc_IN(PC_Count), .Inc_OUT(incrementer_1_inc_out), .Cout(Cout));
  not not_6 (not_6_out, Cout);

  // Notes on the sheet:
  //   Ajout Obligatoire de délais car l'écriture dans les registre s'éffectue sur les fronts montants
endmodule

module V1_5 (
  input  [11:0] Manual_Command,
  input  Manal_Input,
  input  Enable,
  input  [3:0] Input,
  input  [3:0] Set_R1,
  input  [3:0] Set_R0,
  output [5:0] out_7
);

  wire and_3_out, and_4_out, automate_ctrl_entry_1_p2, automate_ctrl_entry_1_p3, automate_ctrl_entry_1_p5,
       automate_ctrl_entry_1_p6, automate_ctrl_entry_1_p8, automate_ctrl_entry_1_p9, clock_1_out, Ena_out,
       L_out, MR_out, not_1_out, or_2_out, or_3_out, or_4_out, or_5_out, R_2_out, R_out;
  wire [1:0] registre_selection_simplified_1_p2;
  wire [3:0] alu_4bits_simplified_1_p5, alu_input_selecter_simplified_1_s, alu_input_selecter_simplified_2_s,
       alu_input_selecter_simplified_comp_1_s, and_5_out, clocked_register_4_1_output, ctrl_v2_1_operation,
       inc_registre_1_pc_count, or_1_out, ram_1_data_out, registre_selection_simplified_1_p3,
       registre_selection_simplified_1_p6, registre_selection_simplified_1_p7,
       registre_selection_simplified_1_p8;
  wire [3:3] Force_set_Memory_out, or_6_out;
  wire [11:0] multiplexer_1_out, rom_1_data;

  Alu_input_selecter_simplified alu_input_selecter_simplified_1 (
    .S(alu_input_selecter_simplified_1_s), .R1(registre_selection_simplified_1_p7),
    .R0(registre_selection_simplified_1_p6), .Selection(registre_selection_simplified_1_p2), .ENABLE(1'b1));  // open: R3, R2
  assign or_1_out = ram_1_data_out | Input | and_5_out;  // OR_Gate or_1, 4 bits wide
  Button R (.out(R_out));
  or or_2 (or_2_out, R_out, automate_ctrl_entry_1_p8);
  Button MR (.out(MR_out));
  // Registre_Selection_simplified registre_selection_simplified_1: pin names not known; wires that end beside it: or_1_out, registre_selection_simplified_1_p2, registre_selection_simplified_1_p3, MR_out, or_2_out, registre_selection_simplified_1_p6, registre_selection_simplified_1_p7, registre_selection_simplified_1_p8
  assign registre_selection_simplified_1_p3 = Set_R1 & {4{Force_set_Memory_out[3]}};  // AND_Gate and_1, 4 bits wide
  assign registre_selection_simplified_1_p8 = {4{Force_set_Memory_out[3]}} & Set_R0;  // AND_Gate and_2, 4 bits wide
  Button Force_set_Memory (.out(Force_set_Memory_out[3]));
  or or_3 (or_3_out, MR_out, automate_ctrl_entry_1_p2);
  Ram ram_1 (
    .Data_in(alu_input_selecter_simplified_1_s), .Write(automate_ctrl_entry_1_p5), .Address(out_7),
    .Reset_writing_state(or_3_out), .Data_out(ram_1_data_out), .CLK(clock_1_out),
    .Enable_output(automate_ctrl_entry_1_p3));
  Hex_Digit_Display hex_digit_display_1 (.value(registre_selection_simplified_1_p6));  // open: dp
  Hex_Digit_Display hex_digit_display_2 (.value(registre_selection_simplified_1_p7));  // open: dp
  or or_4 (or_4_out, Enable, automate_ctrl_entry_1_p9);
  Alu_input_selecter_simplified alu_input_selecter_simplified_2 (
    .S(alu_input_selecter_simplified_2_s), .R1(registre_selection_simplified_1_p7),
    .R0(registre_selection_simplified_1_p6), .Selection(out_7[5:4]), .ENABLE(or_4_out));  // open: R3, R2
  Alu_input_selecter_simplified_comp alu_input_selecter_simplified_comp_1 (
    .S(alu_input_selecter_simplified_comp_1_s), .R1(registre_selection_simplified_1_p7),
    .R0(registre_selection_simplified_1_p6), .Selection(out_7[3:2]), .Complement(out_7[1]), .ENABLE(or_4_out));  // open: R3, R2
  and and_3 (and_3_out, automate_ctrl_entry_1_p2, not_1_out);
  Inc_Registre inc_registre_1 (.PC_Count(inc_registre_1_pc_count), .Outpin(and_3_out));  // open: Cout
  not not_1 (not_1_out, Manal_Input);
  Hex_Digit_Display hex_digit_display_3 (.value(alu_input_selecter_simplified_comp_1_s));  // open: dp
  Multiplexer #(.width(12)) multiplexer_1 (
    .in0(rom_1_data), .in1(Manual_Command), .out(multiplexer_1_out), .sel(Manal_Input));  // open: en
  CTRL_V2 ctrl_v2_1 (
    .Rin_12(multiplexer_1_out), .Operation(ctrl_v2_1_operation), .A(out_7[5:4]),
    .Res(registre_selection_simplified_1_p2), .Ext(out_7[1:0]), .B(out_7[3:2]));
  and and_4 (and_4_out, out_7[0], automate_ctrl_entry_1_p9);
  Hex_Digit_Display hex_digit_display_4 (.value(alu_input_selecter_simplified_2_s));  // open: dp
  ROM #(.addrWidth(4), .dataWidth(12)) rom_1 (.addr(inc_registre_1_pc_count), .data(rom_1_data));  // open: sel
  // Alu_4bits_simplified alu_4bits_simplified_1: pin names not known; wires that end beside it: alu_input_selecter_simplified_2_s, alu_input_selecter_simplified_comp_1_s, and_4_out, ctrl_v2_1_operation[1:0], alu_4bits_simplified_1_p5
  Button R_2 (.out(R_2_out));
  or or_5 (or_5_out, R_2_out, automate_ctrl_entry_1_p2);
  Hex_Digit_Display hex_digit_display_5 (.value(alu_4bits_simplified_1_p5));  // open: dp
  Hex_Digit_Display hex_digit_display_6 (.value(clocked_register_4_1_output));  // open: dp
  Clocked_register_4 clocked_register_4_1 (
    .Set_4(alu_4bits_simplified_1_p5), .Output(clocked_register_4_1_output), .Reset(or_5_out),
    .CLK(clock_1_out));
  Button Ena (.out(Ena_out));
  or or_6 (or_6_out[3], Ena_out, automate_ctrl_entry_1_p6);
  assign and_5_out = clocked_register_4_1_output & {4{or_6_out[3]}};  // AND_Gate and_5, 4 bits wide
  Clock clock_1 (.out(clock_1_out));
  Button L (.out(L_out));
  // Automate_ctrl_Entry automate_ctrl_entry_1: pin names not known; wires that end beside it: L_out, automate_ctrl_entry_1_p2, automate_ctrl_entry_1_p3, clock_1_out, automate_ctrl_entry_1_p5, automate_ctrl_entry_1_p6, ctrl_v2_1_operation[3:2], automate_ctrl_entry_1_p8, automate_ctrl_entry_1_p9

  // Notes on the sheet:
  //   Utilisé comme Mux 4
  //   Visualisation IMM
  //   contents of rom_1 (hex, n*v repeats v):
  //   4 800 841 144 842
  //   Registre temporaire
  //   Launch
  //   0 : Inactif
  //   1 : ALU IN ENABLE
  //   2 : Reset registre cible
  //   3 : Mise en mémoire ( ENABLE sortie ALU)
  //   4 : Flush (reset memoire tempo et reset automate
endmodule

module flags (
  input  CLK,
  input  [3:0] Alu_Res,
  input  Cout_In,
  input  Cin_In,
  output NULL,
  output NEGATIF,
  output OVERFLOW
);

  wire and_1_out, and_2_out, not_1_out, not_2_out, not_3_out, or_1_out;

  not not_1 (not_1_out, Cout_In);
  not not_2 (not_2_out, Cin_In);
  or or_1 (or_1_out, Alu_Res[0], Alu_Res[1], Alu_Res[2], Alu_Res[3]);
  and and_1 (and_1_out, not_1_out, Cin_In);
  and and_2 (and_2_out, Cout_In, not_2_out);
  not not_3 (not_3_out, or_1_out);
  D_Flip_Flop #(.trigger("falling")) d_ff_1 (.clk(CLK), .D(not_3_out), .Q(NULL));  // open: Qn, preset, en, reset
  D_Flip_Flop #(.trigger("falling")) d_ff_2 (.clk(CLK), .D(and_1_out), .Q(NEGATIF));  // open: Qn, preset, en, reset
  D_Flip_Flop #(.trigger("falling")) d_ff_3 (.clk(CLK), .D(and_2_out), .Q(OVERFLOW));  // open: Qn, preset, en, reset
endmodule
